# Fritzing sketch sketch (saved by Fritzing 0.9.10b)
breadboards: 1

parts:
  Mod1 = Amica NodeMCU DEVKIT 1.0
  RGB_SMD_LED1 = SMD RGB LED (WS2812) [package=5050]

nets:
  N1: Mod1.pin1, Mod1.pin_10, Mod1.pin_26
  N2: Mod1.pin2, Mod1.pin_9, Mod1.pin_25, Mod1.pin_29, RGB_SMD_LED1.VSS
  N3: Mod1.pin_12, RGB_SMD_LED1.DIn
  N4: Mod1.pin_30, RGB_SMD_LED1.VCC
